# Fritzing sketch Huzzah DB25 R3 (saved by Fritzing 0.9.3b)
circuit board: 5.47751cm x 3.58998cm
breadboards: 1

parts:
  U1 = RS232 Transceiver [package=so016]
  Feather_Huzzah_ESP8266 = Adafruit Feather HUZZAH ESP8266 [part_number="Adafruit #2821"]
  Pad2 = Pad [width=1.9865715392465519 height=3.9346852017819947 connect=center]
  Pad3 = Pad [width=1.9865715392465519 height=3.9346852017819947 connect=center]
  Pad4 = Pad [width=1.9865715392465519 height=3.9346852017819947 connect=center]  # not connected
  Pad5 = Pad [width=1.9865715392465519 height=3.9346852017819947 connect=center]  # not connected
  Pad6 = Pad [width=1.9865715392465519 height=3.9346852017819947 connect=center]  # not connected
  Pad7 = Pad [width=1.9865715392465519 height=3.9346852017819947 connect=center]  # not connected
  Pad8 = Pad [width=1.9865715392465519 height=3.9346852017819947 connect=center]  # not connected
  Pad9 = Pad [width=1.9865715392465519 height=3.9346852017819947 connect=center]  # not connected
  Pad10 = Pad [width=1.9865715392465519 height=3.9346852017819947 connect=center]  # not connected
  Pad11 = Pad [width=1.9865715392465519 height=3.9346852017819947 connect=center]  # not connected
  Pad12 = Pad [width=1.9865715392465519 height=3.9346852017819947 connect=center]  # not connected
  13 = Pad [width=1.9865715392465519 height=3.9346852017819947 connect=center]  # not connected
  1 = Pad [width=1.9865715392465519 height=3.9346852017819947 connect=center]
  GND = single row smd female pin header, 1 pin [form="♀ (female)"]
  TX = single row smd female pin header, 1 pin [form="♀ (female)"]
  RX = single row smd female pin header, 1 pin [form="♀ (female)"]
  Pad20 = Pad [width=1.9865715392465519 height=3.9346852017819947 connect=center]  # not connected
  Pad18 = Pad [width=1.9865715392465519 height=3.9346852017819947 connect=center]  # not connected
  25 = Pad [width=1.9865715392465519 height=3.9346852017819947 connect=center]  # not connected
  Pad15 = Pad [width=1.9865715392465519 height=3.9346852017819947 connect=center]  # not connected
  Pad14 = Pad [width=1.9865715392465519 height=3.9346852017819947 connect=center]  # not connected
  Pad13 = Pad [width=1.9865715392465519 height=3.9346852017819947 connect=center]  # not connected
  Pad17 = Pad [width=1.9865715392465519 height=3.9346852017819947 connect=center]  # not connected
  Pad19 = Pad [width=1.9865715392465519 height=3.9346852017819947 connect=center]  # not connected
  Pad22 = Pad [width=1.9865715392465519 height=3.9346852017819947 connect=center]  # not connected
  Pad16 = Pad [width=1.9865715392465519 height=3.9346852017819947 connect=center]  # not connected
  14 = Pad [width=1.9865715392465519 height=3.9346852017819947 connect=center]  # not connected
  Pad21 = Pad [width=1.9865715392465519 height=3.9346852017819947 connect=center]  # not connected

nets:
  N1: U1.T1IN, Feather_Huzzah_ESP8266.GPIO5/SCL
  N2: U1.R1OUT, Pad3.pad, RX.pin1
  N3: U1.R1IN, Feather_Huzzah_ESP8266.GPIO4/SDA
  N4: U1.T1OUT, Pad2.pad, TX.pin1
  GND: U1.GND, Feather_Huzzah_ESP8266.GND, 1.pad, GND.pin1

custom parts:
  Adafruit Feather HUZZAH ESP8266: his is the Adafruit Feather HUZZAH ESP8266 - our take on an 'all-in-one' ESP8266 WiFi development board with built in USB and battery charging. Its an ESP8266 WiFi module with all the extras you need, ready to rock! We have other boards in the Feather family, check'em out here. At the Feather HUZZAH's heart is an ESP8266 WiFi microcontroller clocked at 80 MHz and at 3.3V logic. This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
