# Fritzing sketch Huzzah DB25 R6 (saved by Fritzing 0.9.3b)
circuit board: 5.52539cm x 4.31406cm
breadboards: 1

parts:
  Feather_Huzzah_ESP8266 = Adafruit Feather HUZZAH ESP8266 [part_number="Adafruit #2821"]
  MAX3232 = RS232 Transceiver [package=dil16]
  X1 = DB25 [package=db25]  # not connected
  C2 = Ceramic Capacitor [capacitance=100nF package="100 mil [THT, multilayer]"]
  C1 = Ceramic Capacitor [capacitance=100nF package="100 mil [THT, multilayer]"]
  C5 = Ceramic Capacitor [capacitance=100nF package="100 mil [THT, multilayer]"]
  C4 = Ceramic Capacitor [capacitance=100nF package="100 mil [THT, multilayer]"]
  C3 = Ceramic Capacitor [capacitance=100nF package="100 mil [THT, multilayer]"]

nets:
  GND: Feather_Huzzah_ESP8266.GND, MAX3232.GND, C5.1, C4.1, C3.1
  N1: MAX3232.C1+, C1.1
  N2: MAX3232.V+, C3.0
  N3: MAX3232.C1-, C1.0
  N4: MAX3232.C2+, C2.1
  N5: MAX3232.C2-, C2.0
  N6: MAX3232.V-, C4.0
  N7: MAX3232.VCC, C5.0

custom parts:
  Adafruit Feather HUZZAH ESP8266: his is the Adafruit Feather HUZZAH ESP8266 - our take on an 'all-in-one' ESP8266 WiFi development board with built in USB and battery charging. Its an ESP8266 WiFi module with all the extras you need, ready to rock! We have other boards in the Feather family, check'em out here. At the Feather HUZZAH's heart is an ESP8266 WiFi microcontroller clocked at 80 MHz and at 3.3V logic. This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
