# Fritzing sketch Huzzah DB25 R9 (saved by Fritzing 0.9.3b)
circuit board: 5.50943cm x 4.05354cm
breadboards: 1

parts:
  MAX3232 = RS232 Transceiver [package=dil16]
  C2 = Ceramic Capacitor [capacitance=100nF package="100 mil [THT, multilayer]"]
  C1 = Ceramic Capacitor [capacitance=100nF package="100 mil [THT, multilayer]"]
  C5 = Ceramic Capacitor [capacitance=100nF package="100 mil [THT, multilayer]"]
  C4 = Ceramic Capacitor [capacitance=100nF package="100 mil [THT, multilayer]"]
  C3 = Ceramic Capacitor [capacitance=100nF package="100 mil [THT, multilayer]"]
  J1 = female pin header, 16 pins [form="♀ (female)"]  # not connected
  J2 = female pin header, 16 pins [form="♀ (female)"]  # not connected
  X1 = DB25 [package=db25]
  Feather_Huzzah_ESP8266 = Adafruit Feather HUZZAH ESP8266 [part_number="Adafruit #2821"]

nets:
  N1: MAX3232.C1+, C1.1
  N2: MAX3232.V+, C3.0
  N3: MAX3232.C1-, C1.0
  N4: MAX3232.C2+, C2.1
  N5: MAX3232.C2-, C2.0
  N6: MAX3232.V-, C4.0
  N7: MAX3232.T1IN, Feather_Huzzah_ESP8266.GPIO14/SCK
  N8: MAX3232.R1OUT, Feather_Huzzah_ESP8266.GPIO12/MISO
  N9: MAX3232.R1IN, X1.2
  N10: MAX3232.T1OUT, X1.3
  GND: MAX3232.GND, C5.1, C4.1, C3.1, X1.7, Feather_Huzzah_ESP8266.GND
  VCC: MAX3232.VCC, C5.0, Feather_Huzzah_ESP8266.3.3V

notes:
  Feather HUZZAH ESP8266
  Wi-Fi Terminal
  Leif Bloomquist 2017 0v1
  Interface

custom parts:
  Adafruit Feather HUZZAH ESP8266: his is the Adafruit Feather HUZZAH ESP8266 - our take on an 'all-in-one' ESP8266 WiFi development board with built in USB and battery charging. Its an ESP8266 WiFi module with all the extras you need, ready to rock! We have other boards in the Feather family, check'em out here. At the Feather HUZZAH's heart is an ESP8266 WiFi microcontroller clocked at 80 MHz and at 3.3V logic. This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
